# Fritzing sketch Final Project (saved by Fritzing 0.9.5d)
breadboards: 1

parts:
  Part1 = Arduino Uno (Rev3)
  R1 = Resistor [tolerance=±5% resistance=220 package="0805 [SMD]"]
  R2 = Resistor [tolerance=±5% resistance=220 package="0805 [SMD]"]
  R3 = Resistor [tolerance=±5% resistance=220 package="0805 [SMD]"]
  LED1 = RGB LED - (4 legs) [package="5 mm [THT]"]
  S1 = Pushbutton [package="[THT]"]
  U1 = POT [package=pot_mammoth]
  IR1 = TSOP312.., 314.. [package=THT]

nets:
  N1: Part1.A4/SDA, U1.A
  N2: Part1.D9_PWM, R2.Pin_1
  N3: Part1.D10_PWM/SS, R1.Pin_1
  N4: Part1.D11_PWM/MOSI, R3.Pin_1
  N5: Part1.D2, IR1.GND
  N6: Part1.D4, S1.Pin_1, S1.Pin_2
  N7: Part1.5V, U1.E, IR1.Data
  N8: Part1.GND, LED1.common_anode, S1.Pin_3, S1.Pin_4, U1.S, IR1.Vs
  N9: R1.Pin_0, LED1.green_cathode
  N10: R2.Pin_0, LED1.blue_cathode
  N11: R3.Pin_0, LED1.red_cathode
